# Fritzing sketch montage_total (saved by Fritzing 0.9.3b)
breadboards: 3

parts:
  YF-S201_Flow_Meter1 = YF-S201 Water Flow Meter
  Photodiode_2 = S1133 Si Photodiode [package="8mm Ceramic [THT]"]
  R4 = Resistor [tolerance=±5% resistance=10k package=THT]
  R3 = Resistor [tolerance=±5% resistance=10k package=THT]
  Photodiode = S1133 Si Photodiode [package="8mm Ceramic [THT]"]
  Temperature_sensor = Temperature Sensor (Thermistor) [thermistor_type=NTC package=THT]
  Temperature_sensor_2 = Temperature Sensor (Thermistor) [thermistor_type=NTC package=THT]
  R7 = Resistor [tolerance=±5% resistance=2.2k package=THT]
  R8 = Resistor [tolerance=±5% resistance=2.2k package=THT]
  Pressure_sensor = MPX2010 pressure sensor [part_number=MPX]
  Photo_Transistor_Optical_Switch = PHOTOTRANSISTOR REFLECTIVE OBJECT SENSOR [package=qrb1114-side]
  R9 = Resistor [tolerance=±5% resistance=270 package=THT]
  R10 = Resistor [tolerance=±5% resistance=10k package=THT]
  R11 = Resistor [tolerance=±5% resistance=22k package=THT]
  Composant1 = Arduino Mega ADK (Rev3)
  Photoresistor = Photocell (LDR) [package=THT]
  R13 = Resistor [tolerance=±5% resistance=4.7k package=THT]
  MECHANICAL_STOP_2 = PHOTOTRANSISTOR REFLECTIVE OBJECT SENSOR [package=qrb1114-side]
  MECHANICAL_STOP = PHOTOTRANSISTOR REFLECTIVE OBJECT SENSOR [package=qrb1114-side]
  R14 = Resistor [tolerance=±5% resistance=270 package=THT]
  R15 = Resistor [tolerance=±5% resistance=270 package=THT]
  R16 = Resistor [tolerance=±5% resistance=10k package=THT]
  R17 = Resistor [tolerance=±5% resistance=10k package=THT]
  R18 = Resistor [tolerance=±5% resistance=22k package=THT]
  R19 = Resistor [tolerance=±5% resistance=22k package=THT]
  Motor = DC Motor
  Composant2 = Arduino Motor Shield (Rev3)
  VCC1 = Battery block 9V
  Led_wall = LED_BARGRAPH_10 [package=led_bargaph_10]
  LED1 = LED - 3mm [color="Red (633nm)" package="3 mm [THT]"]
  LED2 = LED - 3mm [color="Green (570nm)" package="3 mm [THT]"]
  LED3 = LED - 3mm [color="Red (633nm)" package="3 mm [THT]"]
  LED4 = LED - 3mm [color="Red (633nm)" package="3 mm [THT]"]
  LED5 = LED - 3mm [color="Red (633nm)" package="3 mm [THT]"]
  LED6 = LED - 3mm [color="Green (570nm)" package="3 mm [THT]"]
  R20 = Resistor [tolerance=±5% resistance=1k package="2512 [SMD]"]
  R21 = Resistor [tolerance=±5% resistance=1k package="2512 [SMD]"]
  R22 = Resistor [tolerance=±5% resistance=1k package="2512 [SMD]"]
  R23 = Resistor [tolerance=±5% resistance=1k package="2512 [SMD]"]
  R24 = Resistor [tolerance=±5% resistance=1k package="2512 [SMD]"]
  R25 = Resistor [tolerance=±5% resistance=1k package="2512 [SMD]"]
  R26 = Resistor [tolerance=±5% resistance=1k package="2512 [SMD]"]
  R27 = Resistor [tolerance=±5% resistance=1k package="2512 [SMD]"]
  R28 = Resistor [tolerance=±5% resistance=1k package="2512 [SMD]"]
  R29 = Resistor [tolerance=±5% resistance=1k package="2512 [SMD]"]
  R30 = Resistor [tolerance=±5% resistance=1k package="2512 [SMD]"]
  R31 = Resistor [tolerance=±5% resistance=1k package="2512 [SMD]"]
  R32 = Resistor [tolerance=±5% resistance=1k package="2512 [SMD]"]
  R33 = Resistor [tolerance=±5% resistance=1k package="2512 [SMD]"]
  R34 = Resistor [tolerance=±5% resistance=1k package="2512 [SMD]"]
  R35 = Resistor [tolerance=±5% resistance=1k package="2512 [SMD]"]
  Emergency_switch = SWITCH-MOMENTARY-2 [package=tactile_switch_smd-2]
  S2 = SPST Switch [package=r_sw_th]

nets (from the schematic view):
  N1: YF-S201_Flow_Meter1.SIG, Composant1.D20/SDA
  GND: YF-S201_Flow_Meter1.GND, R4.Pin_0, R3.Pin_0, R7.Pin_1, R8.Pin_0, Pressure_sensor.GND, Photo_Transistor_Optical_Switch.E, Photo_Transistor_Optical_Switch.K, R11.Pin_1, Composant1.GND, R13.Pin_1, MECHANICAL_STOP_2.E, MECHANICAL_STOP_2.K, MECHANICAL_STOP.E, MECHANICAL_STOP.K, R18.Pin_1, R19.Pin_1, VCC1.-, Led_wall.J_C, Led_wall.I_C, Led_wall.H_C, Led_wall.G_C, Led_wall.F_C, Led_wall.E_C, Led_wall.D_C, Led_wall.C_C, Led_wall.B_C, Led_wall.A_C, LED1.cathode, LED2.cathode, LED3.cathode, LED4.cathode, LED5.cathode, LED6.cathode, Emergency_switch.2
  VCC: YF-S201_Flow_Meter1.VCC, R10.Pin_1, Composant1.IOREF, Composant1.5V, Photoresistor.pin_0, R14.Pin_0, R15.Pin_0, R16.Pin_1, R17.Pin_1, R20.Pin_1, R21.Pin_1, R22.Pin_1, R23.Pin_1, R24.Pin_1, R25.Pin_1, R26.Pin_1, R27.Pin_1, R28.Pin_1, R29.Pin_1, R30.Pin_1, R31.Pin_1, R32.Pin_1, R33.Pin_1, R34.Pin_1, R35.Pin_1
  N2: Photodiode_2.cathode, R4.Pin_1, Composant1.A6
  N3: Photodiode_2.anode, Photodiode.anode, Temperature_sensor.pin_0, Temperature_sensor_2.pin_1, Pressure_sensor.Vs, Composant1.3V3
  N4: R3.Pin_1, Photodiode.cathode, Composant1.A5
  N5: Temperature_sensor.pin_1, R7.Pin_0, Composant1.A12
  N6: Temperature_sensor_2.pin_0, R8.Pin_1, Composant1.A13
  N7: Pressure_sensor.V_out_+, Composant1.A4
  N8: Photo_Transistor_Optical_Switch.A, R9.Pin_1
  N9: Photo_Transistor_Optical_Switch.C, R10.Pin_0, R11.Pin_0, Composant1.D22
  N10: Composant1.A7, Photoresistor.pin_1, R13.Pin_0
  N11: Composant1.D19/RX1, MECHANICAL_STOP_2.C, R16.Pin_0, R18.Pin_0
  N12: Composant1.D18/TX1, MECHANICAL_STOP.C, R17.Pin_0, R19.Pin_0
  N13: Composant1.RESET, Emergency_switch.1
  N14: Composant1.VIN, S2.P
  N15: Composant1.D30, Led_wall.F_A, R25.Pin_0
  N16: Composant1.D31, Led_wall.G_A, R26.Pin_0
  N17: Composant1.D32, Led_wall.H_A, R27.Pin_0
  N18: Composant1.D33, Led_wall.I_A, R28.Pin_0
  N19: Composant1.D34, Led_wall.J_A, R29.Pin_0
  N20: Composant1.D35, Led_wall.A_A, R20.Pin_0
  N21: Composant1.D36, Led_wall.B_A, R21.Pin_0
  N22: Composant1.D37, Composant1.D38, Led_wall.C_A, R22.Pin_0
  N23: Composant1.D39, Led_wall.E_A, R24.Pin_0
  N24: Composant1.D40, LED1.anode, R32.Pin_0
  N25: Composant1.D41, LED2.anode, R30.Pin_0
  N26: Composant1.D42, LED3.anode, R33.Pin_0
  N27: Composant1.D43, LED4.anode, R34.Pin_0
  N28: Composant1.D44, LED5.anode, R35.Pin_0
  N29: Composant1.D45, LED6.anode, R31.Pin_0
  N30: MECHANICAL_STOP_2.A, R14.Pin_1
  N31: MECHANICAL_STOP.A, R15.Pin_1
  N32: Motor.pin_1, Composant2.A+
  N33: Motor.pin_2, Composant2.A-
  N34: VCC1.+, S2.O
  N35: Led_wall.D_A, R23.Pin_0

custom parts:
  YF-S201 Water Flow Meter: The YF-S201 Flow Meter. The input voltage is 5V to 24V (DC).
